// Logisim project ULA.circ as structural Verilog: 11 circuits, main circuit main
module main (
  input  in_1,
  input  [2:0] in_2,
  input  [2:0] in_3
);

  wire somador_completo_1_carry, somador_completo_2_carry, subtrador_completo_1_bout,
       subtrador_completo_2_bout;
  wire [3:0] somador_completo_1_r, subtrador_completo_1_r;

  somador_completo somador_completo_1 (
    .C(in_1), .A(in_2[0]), .B(in_3[0]), .R(somador_completo_1_r[0]), .Carry(somador_completo_1_carry));
  somador_completo somador_completo_2 (
    .C(somador_completo_1_carry), .A(in_2[1]), .B(in_3[1]), .R(somador_completo_1_r[1]),
    .Carry(somador_completo_2_carry));
  somador_completo somador_completo_3 (
    .C(somador_completo_2_carry), .A(in_2[2]), .B(in_3[2]), .R(somador_completo_1_r[2]),
    .Carry(somador_completo_1_r[3]));
  subtrador_completo subtrador_completo_1 (
    .Bin(in_1), .A(in_2[0]), .B(in_3[0]), .R(subtrador_completo_1_r[0]), .Bout(subtrador_completo_1_bout));
  subtrador_completo subtrador_completo_2 (
    .Bin(subtrador_completo_1_bout), .A(in_2[1]), .B(in_3[1]), .R(subtrador_completo_1_r[1]),
    .Bout(subtrador_completo_2_bout));
  subtrador_completo subtrador_completo_3 (
    .Bin(subtrador_completo_2_bout), .A(in_2[2]), .B(in_3[2]), .R(subtrador_completo_1_r[2]),
    .Bout(subtrador_completo_1_r[3]));
  Hex_Digit_Display hex_digit_display_1 (.value(somador_completo_1_r));  // open: dp
  Hex_Digit_Display hex_digit_display_2 (.value(subtrador_completo_1_r));  // open: dp
endmodule

// Som
module somador_completo (
  input  C,
  input  A,
  input  B,
  output R,
  output Carry
);

  wire and_1_out, and_2_out, xor_1_out, xor_2_out;

  xor xor_1 (xor_1_out, A, B);
  xor xor_2 (xor_2_out, A, B);
  xor xor_3 (R, xor_1_out, C);
  and and_1 (and_1_out, xor_2_out, C);
  or or_1 (Carry, and_1_out, and_2_out);
  and and_2 (and_2_out, A, B);
endmodule

// Sub
module subtrador_completo (
  input  Bin,
  input  A,
  input  B,
  output R,
  output Bout
);

  wire and_1_out, and_2_out, not_1_out, xor_1_out, xor_3_out;

  xor xor_1 (xor_1_out, A, B);
  xor xor_2 (R, xor_1_out, Bin);
  xor xor_3 (xor_3_out, B, Bin);
  and and_1 (and_1_out, xor_3_out, not_1_out);
  not not_1 (not_1_out, A);
  and and_2 (and_2_out, B, Bin);
  or or_1 (Bout, and_1_out, and_2_out);
endmodule

module teste (
  input  A,
  input  B,
  input  C,
  input  [7:0] in_4,
  input  [2:0] in_5,
  output R,
  output out_7,
  output [7:0] out_8
);

  wire and_1_out, and_2_out, not_1_out, xor_1_out, xor_3_out;

  xor xor_1 (xor_1_out, A, B);
  xor xor_2 (R, xor_1_out, C);
  xor xor_3 (xor_3_out, B, C);
  not not_1 (not_1_out, A);
  and and_1 (and_1_out, B, C);
  and and_2 (and_2_out, xor_3_out, not_1_out);
  or or_1 (out_7, and_2_out, and_1_out);
  Shifter shifter_1 (.in(in_4), .\dist (in_5), .out(out_8));
endmodule

module multiplicador (
  input  [7:0] in_1,
  input  [7:0] in_2,
  input  in_3,
  output out_4,
  output out_5,
  output out_6,
  output out_7,
  output out_8,
  output out_9,
  output out_10,
  output out_11,
  output out_12,
  output out_13,
  output out_14,
  output out_15,
  output out_16,
  output out_17,
  output out_18,
  output out_19
);

  wire and_1_out, and_2_out, button_1_out, clock_1_out, multiplexer_1_out, not_1_out, or_1_out,
       somador_de_16_bits_1_r0, somador_de_16_bits_1_r1, somador_de_16_bits_1_r2, somador_de_16_bits_1_r3,
       somador_de_16_bits_1_r4, somador_de_16_bits_1_r5, somador_de_16_bits_1_r6, somador_de_16_bits_1_r7,
       somador_de_16_bits_1_r8, somador_de_16_bits_1_r9, somador_de_16_bits_1_r10, somador_de_16_bits_1_r11,
       somador_de_16_bits_1_r12, somador_de_16_bits_1_r13, somador_de_16_bits_1_r14, somador_de_16_bits_1_r15;
  wire [2:0] Contador_q;
  wire [7:0] and_10_out;
  wire [15:0] shifter_1_out;

  Clock clock_1 (.out(clock_1_out));
  and and_1 (and_1_out, clock_1_out, not_1_out);
  memoria_16_bits memoria_16_bits_1 (
    .clock(clock_1_out), .reset(button_1_out), .E15(somador_de_16_bits_1_r15),
    .E14(somador_de_16_bits_1_r14), .E13(somador_de_16_bits_1_r13), .E12(somador_de_16_bits_1_r12),
    .E11(somador_de_16_bits_1_r11), .E10(somador_de_16_bits_1_r10), .E9(somador_de_16_bits_1_r9),
    .E8(somador_de_16_bits_1_r8), .E7(somador_de_16_bits_1_r7), .E6(somador_de_16_bits_1_r6),
    .E5(somador_de_16_bits_1_r5), .E4(somador_de_16_bits_1_r4), .E3(somador_de_16_bits_1_r3),
    .E2(somador_de_16_bits_1_r2), .E1(somador_de_16_bits_1_r1), .E0(somador_de_16_bits_1_r0), .S15(out_4),
    .S14(out_5), .S13(out_6), .S12(out_7), .S11(out_8), .S10(out_9), .S9(out_10), .S8(out_11), .S7(out_12),
    .S6(out_13), .S5(out_14), .S4(out_15), .S3(out_16), .S2(out_17), .S1(out_18), .S0(out_19));
  Counter #(.width(3), .max('h7)) Contador (
    .Q(Contador_q), .clk(and_1_out), .clr(button_1_out));  // open: load, D, count, carry
  Button button_1 (.out(button_1_out));
  not not_1 (not_1_out, and_2_out);
  or or_1 (or_1_out, Contador_q[2], Contador_q[1], Contador_q[0]);
  and and_2 (and_2_out, Contador_q[2], Contador_q[1], Contador_q[0]);
  Multiplexer #(.select(3)) multiplexer_1 (
    .in0(in_2[0]), .in1(in_2[1]), .in2(in_2[2]), .in3(in_2[3]), .in4(in_2[4]), .in5(in_2[5]), .in6(in_2[6]),
    .in7(in_2[7]), .out(multiplexer_1_out), .sel(Contador_q), .en(in_3));
  and and_3 (and_10_out[7], in_1[7], multiplexer_1_out);
  and and_4 (and_10_out[6], in_1[6], multiplexer_1_out);
  and and_5 (and_10_out[5], in_1[5], multiplexer_1_out);
  and and_6 (and_10_out[4], in_1[4], multiplexer_1_out);
  somador_de_16_bits somador_de_16_bits_1 (
    .A15(out_4), .B15(shifter_1_out[15]), .A14(out_5), .B14(shifter_1_out[14]), .A13(out_6),
    .B13(shifter_1_out[13]), .A12(out_7), .B12(shifter_1_out[12]), .A11(out_8), .B11(shifter_1_out[11]),
    .A10(out_9), .B10(shifter_1_out[10]), .A9(out_10), .B9(shifter_1_out[9]), .A8(out_11),
    .B8(shifter_1_out[8]), .A7(out_12), .B7(shifter_1_out[7]), .A6(out_13), .B6(shifter_1_out[6]),
    .A5(out_14), .B5(shifter_1_out[5]), .A4(out_15), .B4(shifter_1_out[4]), .A3(out_16),
    .B3(shifter_1_out[3]), .A2(out_17), .B2(shifter_1_out[2]), .A1(out_18), .B1(shifter_1_out[1]),
    .A0(out_19), .B0(shifter_1_out[0]), .R15(somador_de_16_bits_1_r15), .R14(somador_de_16_bits_1_r14),
    .R13(somador_de_16_bits_1_r13), .R12(somador_de_16_bits_1_r12), .R11(somador_de_16_bits_1_r11),
    .R10(somador_de_16_bits_1_r10), .R9(somador_de_16_bits_1_r9), .R8(somador_de_16_bits_1_r8),
    .R7(somador_de_16_bits_1_r7), .R6(somador_de_16_bits_1_r6), .R5(somador_de_16_bits_1_r5),
    .R4(somador_de_16_bits_1_r4), .R3(somador_de_16_bits_1_r3), .R2(somador_de_16_bits_1_r2),
    .R1(somador_de_16_bits_1_r1), .R0(somador_de_16_bits_1_r0));  // open: C
  and and_7 (and_10_out[2], in_1[2], multiplexer_1_out);
  and and_8 (and_10_out[3], in_1[3], multiplexer_1_out);
  Shifter #(.width(16)) shifter_1 (.in({{8{1'b0}}, and_10_out}), .\dist ({1'b0, Contador_q}), .out(shifter_1_out));
  Hex_Digit_Display hex_digit_display_1 (.value({out_4, out_5, out_6, out_7}));  // open: dp
  and and_9 (and_10_out[1], in_1[1], multiplexer_1_out);
  and and_10 (and_10_out[0], in_1[0], multiplexer_1_out);
  Hex_Digit_Display hex_digit_display_2 (.value({out_8, out_9, out_10, out_11}));  // open: dp
  Hex_Digit_Display hex_digit_display_3 (.value({out_12, out_13, out_14, out_15}));  // open: dp
  Hex_Digit_Display hex_digit_display_4 (.value({out_16, out_17, out_18, out_19}));  // open: dp
endmodule

module somador_4_bits (
  input  A3,
  input  B3,
  input  A2,
  input  B2,
  input  A1,
  input  B1,
  input  A0,
  input  B0,
  output C,
  output R3,
  output R2,
  output R1,
  output R0
);

  wire somador_completo_2_carry, somador_completo_3_carry, somador_completo_4_carry;

  somador_completo somador_completo_1 (.C(somador_completo_3_carry), .A(B3), .B(A3), .R(R3), .Carry(C));
  somador_completo somador_completo_2 (
    .C(somador_completo_4_carry), .A(B1), .B(A1), .R(R1), .Carry(somador_completo_2_carry));
  somador_completo somador_completo_3 (
    .C(somador_completo_2_carry), .A(B2), .B(A2), .R(R2), .Carry(somador_completo_3_carry));
  somador_completo somador_completo_4 (.C(1'b0), .A(B0), .B(A0), .R(R0), .Carry(somador_completo_4_carry));
endmodule

// Somador
module somador_de_16_bits (
  input  A15,
  input  B15,
  input  A14,
  input  B14,
  input  A13,
  input  B13,
  input  A12,
  input  B12,
  input  A11,
  input  B11,
  input  A10,
  input  B10,
  input  A9,
  input  B9,
  input  A8,
  input  B8,
  input  A7,
  input  B7,
  input  A6,
  input  B6,
  input  A5,
  input  B5,
  input  A4,
  input  B4,
  input  A3,
  input  B3,
  input  A2,
  input  B2,
  input  A1,
  input  B1,
  input  A0,
  input  B0,
  output C,
  output R15,
  output R14,
  output R13,
  output R12,
  output R11,
  output R10,
  output R9,
  output R8,
  output R7,
  output R6,
  output R5,
  output R4,
  output R3,
  output R2,
  output R1,
  output R0
);

  wire somador_completo_2_carry, somador_completo_3_carry, somador_completo_4_carry,
       somador_completo_5_carry, somador_completo_6_carry, somador_completo_7_carry,
       somador_completo_8_carry, somador_completo_9_carry, somador_completo_10_carry,
       somador_completo_11_carry, somador_completo_12_carry, somador_completo_13_carry,
       somador_completo_14_carry, somador_completo_15_carry, somador_completo_16_carry;

  somador_completo somador_completo_1 (.C(somador_completo_2_carry), .A(B15), .B(A15), .R(R15), .Carry(C));
  somador_completo somador_completo_2 (
    .C(somador_completo_3_carry), .A(B14), .B(A14), .R(R14), .Carry(somador_completo_2_carry));
  somador_completo somador_completo_3 (
    .C(somador_completo_4_carry), .A(B13), .B(A13), .R(R13), .Carry(somador_completo_3_carry));
  somador_completo somador_completo_4 (
    .C(somador_completo_5_carry), .A(B12), .B(A12), .R(R12), .Carry(somador_completo_4_carry));
  somador_completo somador_completo_5 (
    .C(somador_completo_6_carry), .A(B11), .B(A11), .R(R11), .Carry(somador_completo_5_carry));
  somador_completo somador_completo_6 (
    .C(somador_completo_7_carry), .A(B10), .B(A10), .R(R10), .Carry(somador_completo_6_carry));
  somador_completo somador_completo_7 (
    .C(somador_completo_8_carry), .A(B9), .B(A9), .R(R9), .Carry(somador_completo_7_carry));
  somador_completo somador_completo_8 (
    .C(somador_completo_9_carry), .A(B8), .B(A8), .R(R8), .Carry(somador_completo_8_carry));
  somador_completo somador_completo_9 (
    .C(somador_completo_10_carry), .A(B7), .B(A7), .R(R7), .Carry(somador_completo_9_carry));
  somador_completo somador_completo_10 (
    .C(somador_completo_11_carry), .A(B6), .B(A6), .R(R6), .Carry(somador_completo_10_carry));
  somador_completo somador_completo_11 (
    .C(somador_completo_12_carry), .A(B5), .B(A5), .R(R5), .Carry(somador_completo_11_carry));
  somador_completo somador_completo_12 (
    .C(somador_completo_13_carry), .A(B4), .B(A4), .R(R4), .Carry(somador_completo_12_carry));
  somador_completo somador_completo_13 (
    .C(somador_completo_14_carry), .A(B3), .B(A3), .R(R3), .Carry(somador_completo_13_carry));
  somador_completo somador_completo_14 (
    .C(somador_completo_15_carry), .A(B2), .B(A2), .R(R2), .Carry(somador_completo_14_carry));
  somador_completo somador_completo_15 (
    .C(somador_completo_16_carry), .A(B1), .B(A1), .R(R1), .Carry(somador_completo_15_carry));
  somador_completo somador_completo_16 (.C(1'b0), .A(B0), .B(A0), .R(R0), .Carry(somador_completo_16_carry));
endmodule

// Memória
module memoria_16_bits (
  input  E15,
  input  E14,
  input  E13,
  input  E12,
  input  E11,
  input  E10,
  input  E9,
  input  E8,
  input  E7,
  input  E6,
  input  E5,
  input  E4,
  input  E3,
  input  E2,
  input  E1,
  input  E0,
  input  clock,
  input  reset,
  output S15,
  output S14,
  output S13,
  output S12,
  output S11,
  output S10,
  output S9,
  output S8,
  output S7,
  output S6,
  output S5,
  output S4,
  output S3,
  output S2,
  output S1,
  output S0
);

  D_Flip_Flop d_ff_1 (.clk(clock), .D(E15), .Q(S15), .preset(1'b0), .en(1'b1), .reset(reset));  // open: Qn
  D_Flip_Flop d_ff_2 (.clk(clock), .D(E14), .Q(S14), .preset(1'b0), .en(1'b1), .reset(reset));  // open: Qn
  D_Flip_Flop d_ff_3 (.clk(clock), .D(E13), .Q(S13), .preset(1'b0), .en(1'b1), .reset(reset));  // open: Qn
  D_Flip_Flop d_ff_4 (.clk(clock), .D(E12), .Q(S12), .preset(1'b0), .en(1'b1), .reset(reset));  // open: Qn
  D_Flip_Flop d_ff_5 (.clk(clock), .D(E11), .Q(S11), .preset(1'b0), .en(1'b1), .reset(reset));  // open: Qn
  D_Flip_Flop d_ff_6 (.clk(clock), .D(E10), .Q(S10), .preset(1'b0), .en(1'b1), .reset(reset));  // open: Qn
  D_Flip_Flop d_ff_7 (.clk(clock), .D(E9), .Q(S9), .preset(1'b0), .en(1'b1), .reset(reset));  // open: Qn
  D_Flip_Flop d_ff_8 (.clk(clock), .D(E8), .Q(S8), .preset(1'b0), .en(1'b1), .reset(reset));  // open: Qn
  D_Flip_Flop d_ff_9 (.clk(clock), .D(E7), .Q(S7), .preset(1'b0), .en(1'b1), .reset(reset));  // open: Qn
  D_Flip_Flop d_ff_10 (.clk(clock), .D(E6), .Q(S6), .preset(1'b0), .en(1'b1), .reset(reset));  // open: Qn
  D_Flip_Flop d_ff_11 (.clk(clock), .D(E5), .Q(S5), .preset(1'b0), .en(1'b1), .reset(reset));  // open: Qn
  D_Flip_Flop d_ff_12 (.clk(clock), .D(E4), .Q(S4), .preset(1'b0), .en(1'b1), .reset(reset));  // open: Qn
  D_Flip_Flop d_ff_13 (.clk(clock), .D(E3), .Q(S3), .preset(1'b0), .en(1'b1), .reset(reset));  // open: Qn
  D_Flip_Flop d_ff_14 (.clk(clock), .D(E2), .Q(S2), .preset(1'b0), .en(1'b1), .reset(reset));  // open: Qn
  D_Flip_Flop d_ff_15 (.clk(clock), .D(E0), .Q(S0), .preset(1'b0), .en(1'b1), .reset(reset));  // open: Qn
  D_Flip_Flop d_ff_16 (.clk(clock), .D(E1), .Q(S1), .preset(1'b0), .en(1'b1), .reset(reset));  // open: Qn
endmodule

module divisor (
  input  [7:0] in_1,
  input  [7:0] in_2
);

  wire and_1_out, button_1_out, clock_1_out, memoria_8_bits_1_s0, memoria_8_bits_1_s1, memoria_8_bits_1_s2,
       memoria_8_bits_1_s3, memoria_8_bits_1_s4, memoria_8_bits_1_s5, memoria_8_bits_1_s6,
       memoria_8_bits_1_s7, multiplexer_1_out, multiplexer_2_out, multiplexer_3_out, multiplexer_4_out,
       multiplexer_5_out, multiplexer_6_out, multiplexer_7_out, multiplexer_8_out, nor_1_out, or_1_out,
       subtrator_16_bits_1_r0, subtrator_16_bits_1_r1, subtrator_16_bits_1_r2, subtrator_16_bits_1_r3,
       subtrator_16_bits_1_r4, subtrator_16_bits_1_r5, subtrator_16_bits_1_r6, subtrator_16_bits_1_r7;
  wire [2:0] Contador_q;

  Clock clock_1 (.out(clock_1_out));
  and and_1 (and_1_out, clock_1_out, or_1_out);
  Counter #(.width(3), .max('h7)) Contador (
    .Q(Contador_q), .clk(and_1_out), .clr(button_1_out));  // open: load, D, count, carry
  Button button_1 (.out(button_1_out));
  nor nor_1 (nor_1_out, Contador_q[2], Contador_q[1], Contador_q[0]);
  or or_1 (or_1_out, memoria_8_bits_1_s0, memoria_8_bits_1_s1, memoria_8_bits_1_s2, memoria_8_bits_1_s3, memoria_8_bits_1_s4, memoria_8_bits_1_s5, memoria_8_bits_1_s6, memoria_8_bits_1_s7);
  memoria_8_bits memoria_8_bits_1 (
    .clock(and_1_out), .reset(button_1_out), .S7(memoria_8_bits_1_s7), .S6(memoria_8_bits_1_s6),
    .S5(memoria_8_bits_1_s5), .S4(memoria_8_bits_1_s4), .S3(memoria_8_bits_1_s3), .S2(memoria_8_bits_1_s2),
    .S1(memoria_8_bits_1_s1), .S0(memoria_8_bits_1_s0), ._7(subtrator_16_bits_1_r7),
    .E6(subtrator_16_bits_1_r6), .E5(subtrator_16_bits_1_r5), .E4(subtrator_16_bits_1_r4),
    .E3(subtrator_16_bits_1_r3), .E2(subtrator_16_bits_1_r2), .E1(subtrator_16_bits_1_r1),
    .E0(subtrator_16_bits_1_r0));
  Multiplexer multiplexer_1 (
    .in0(memoria_8_bits_1_s7), .in1(in_1[7]), .out(multiplexer_1_out), .sel(nor_1_out), .en(1'b1));
  Multiplexer multiplexer_2 (
    .in0(memoria_8_bits_1_s5), .in1(in_1[5]), .out(multiplexer_2_out), .sel(nor_1_out), .en(1'b1));
  Multiplexer multiplexer_3 (
    .in0(memoria_8_bits_1_s6), .in1(in_1[6]), .out(multiplexer_3_out), .sel(nor_1_out), .en(1'b1));
  subtrator_16_bits subtrator_16_bits_1 (
    .A7(in_2[7]), .B7(multiplexer_1_out), .A6(in_2[6]), .B6(multiplexer_3_out), .A5(in_2[5]),
    .B5(multiplexer_2_out), .A4(in_2[4]), .B4(multiplexer_4_out), .A3(in_2[3]), .B3(multiplexer_5_out),
    .A2(in_2[2]), .B2(multiplexer_7_out), .A1(in_2[1]), .B1(multiplexer_6_out), .A0(in_2[0]),
    .B0(multiplexer_8_out), .R7(subtrator_16_bits_1_r7), .R6(subtrator_16_bits_1_r6),
    .R5(subtrator_16_bits_1_r5), .R4(subtrator_16_bits_1_r4), .R3(subtrator_16_bits_1_r3),
    .R2(subtrator_16_bits_1_r2), .R1(subtrator_16_bits_1_r1), .R0(subtrator_16_bits_1_r0));  // open: C
  Multiplexer multiplexer_4 (
    .in0(memoria_8_bits_1_s4), .in1(in_1[4]), .out(multiplexer_4_out), .sel(nor_1_out), .en(1'b1));
  Multiplexer multiplexer_5 (
    .in0(memoria_8_bits_1_s3), .in1(in_1[3]), .out(multiplexer_5_out), .sel(nor_1_out), .en(1'b1));
  Multiplexer multiplexer_6 (
    .in0(memoria_8_bits_1_s1), .in1(in_1[1]), .out(multiplexer_6_out), .sel(nor_1_out), .en(1'b1));
  Multiplexer multiplexer_7 (
    .in0(memoria_8_bits_1_s2), .in1(in_1[2]), .out(multiplexer_7_out), .sel(nor_1_out), .en(1'b1));
  Multiplexer multiplexer_8 (
    .in0(memoria_8_bits_1_s0), .in1(in_1[0]), .out(multiplexer_8_out), .sel(nor_1_out), .en(1'b1));
endmodule

// Subtrator
module subtrator_16_bits (
  input  A7,
  input  B7,
  input  A6,
  input  B6,
  input  A5,
  input  B5,
  input  A4,
  input  B4,
  input  A3,
  input  B3,
  input  A2,
  input  B2,
  input  A1,
  input  B1,
  input  A0,
  input  B0,
  output C,
  output R7,
  output R6,
  output R5,
  output R4,
  output R3,
  output R2,
  output R1,
  output R0
);

  wire subtrador_completo_2_bout, subtrador_completo_3_bout, subtrador_completo_4_bout,
       subtrador_completo_5_bout, subtrador_completo_6_bout, subtrador_completo_7_bout,
       subtrador_completo_8_bout;

  subtrador_completo subtrador_completo_1 (.Bin(subtrador_completo_2_bout), .A(B7), .B(A7), .R(R7), .Bout(C));
  subtrador_completo subtrador_completo_2 (
    .Bin(subtrador_completo_3_bout), .A(B6), .B(A6), .R(R6), .Bout(subtrador_completo_2_bout));
  subtrador_completo subtrador_completo_3 (
    .Bin(subtrador_completo_4_bout), .A(B5), .B(A5), .R(R5), .Bout(subtrador_completo_3_bout));
  subtrador_completo subtrador_completo_4 (
    .Bin(subtrador_completo_6_bout), .A(B4), .B(A4), .R(R4), .Bout(subtrador_completo_4_bout));
  subtrador_completo subtrador_completo_5 (
    .Bin(subtrador_completo_7_bout), .A(B2), .B(A2), .R(R2), .Bout(subtrador_completo_5_bout));
  subtrador_completo subtrador_completo_6 (
    .Bin(subtrador_completo_5_bout), .A(B3), .B(A3), .R(R3), .Bout(subtrador_completo_6_bout));
  subtrador_completo subtrador_completo_7 (
    .Bin(subtrador_completo_8_bout), .A(B1), .B(A1), .R(R1), .Bout(subtrador_completo_7_bout));
  subtrador_completo subtrador_completo_8 (.Bin(1'b0), .A(B0), .B(A0), .R(R0), .Bout(subtrador_completo_8_bout));
endmodule

module memoria_8_bits (
  input  _7,
  input  E6,
  input  E5,
  input  E4,
  input  E3,
  input  E2,
  input  E1,
  input  E0,
  input  clock,
  input  reset,
  output S7,
  output S6,
  output S5,
  output S4,
  output S3,
  output S2,
  output S1,
  output S0
);

  D_Flip_Flop d_ff_1 (.clk(clock), .D(_7), .Q(S7), .preset(reset), .en(1'b1), .reset(1'b0));  // open: Qn
  D_Flip_Flop d_ff_2 (.clk(clock), .D(E6), .Q(S6), .preset(reset), .en(1'b1), .reset(1'b0));  // open: Qn
  D_Flip_Flop d_ff_3 (.clk(clock), .D(E5), .Q(S5), .preset(reset), .en(1'b1), .reset(1'b0));  // open: Qn
  D_Flip_Flop d_ff_4 (.clk(clock), .D(E4), .Q(S4), .preset(reset), .en(1'b1), .reset(1'b0));  // open: Qn
  D_Flip_Flop d_ff_5 (.clk(clock), .D(E3), .Q(S3), .preset(reset), .en(1'b1), .reset(1'b0));  // open: Qn
  D_Flip_Flop d_ff_6 (.clk(clock), .D(E2), .Q(S2), .preset(reset), .en(1'b1), .reset(1'b0));  // open: Qn
  D_Flip_Flop d_ff_7 (.clk(clock), .D(E1), .Q(S1), .preset(reset), .en(1'b1), .reset(1'b0));  // open: Qn
  D_Flip_Flop d_ff_8 (.clk(clock), .D(E0), .Q(S0), .preset(reset), .en(1'b1), .reset(1'b0));  // open: Qn
endmodule
